# Fritzing sketch pow-adapt (saved by Fritzing 0.9.3b)
circuit board: 4.39432cm x 4.54036cm
breadboards: 1

parts:
  HCF4094 = IC, DIP package, 16 pins [chip_label=HCF4094]
  C1 = Capacitor [package=cap-pth-small2]
  From_J21 = shrouded pin header, 20 pins [form="♂ (shrouded male)"]
  4N35 = Optocoupler [package=THT]
  R1 = Resistor [tolerance=±5% resistance=220 package=THT]
  To_POW = female pin header, 6 pins [form="♀ (female)"]
  GND = female pin header, 3 pins [form="♀ (female)"]
  Out = female pin header, 2 pins [form="♀ (female)"]

nets:
  N1: HCF4094.pin1, From_J21.pin17
  N2: HCF4094.pin2, From_J21.pin18
  N3: HCF4094.pin3, From_J21.pin20
  N4: HCF4094.pin4, To_POW.pin3
  N5: HCF4094.pin8, C1.1, From_J21.pin2, From_J21.pin3, From_J21.pin4, From_J21.pin5, From_J21.pin7, From_J21.pin8, From_J21.pin9, From_J21.pin10, 4N35.Pin_4, To_POW.pin2, To_POW.pin4, GND.pin1
  N6: HCF4094.pin15, HCF4094.pin16, C1.2, From_J21.pin1, From_J21.pin6, To_POW.pin1
  N7: 4N35.Pin_1, R1.Pin_0
  N8: 4N35.Pin_2, GND.pin2
  N9: 4N35.Pin_5, Out.pin1, Out.pin2
  N10: R1.Pin_1, To_POW.pin5
  N11: To_POW.pin6, GND.pin3

notes:
  clock
  data
  latch
