# Fritzing sketch row-power-v3 (saved by Fritzing 0.9.3b)
circuit board: 10.3505cm x 6.82996cm
breadboards: 1

parts:
  Teensy_3_2 = Teensy 3.1
  R1 = Resistor [tolerance=±5% resistance=220 package=THT]
  R2 = Resistor [tolerance=±5% resistance=220 package=THT]
  R3 = Resistor [tolerance=±5% resistance=10k package=THT]
  R4 = Resistor [tolerance=±5% resistance=10k package=THT]
  R5 = Resistor [tolerance=±5% resistance=220 package=THT]
  R6 = Resistor [tolerance=±5% resistance=220 package=THT]
  R4_2 = Resistor [tolerance=±5% resistance=220 package=THT]
  C1 = Capacitor Polarized [package=cpol-radial-100uf-25v]
  LED1 = LED - 3mm [color="Red (633nm)" package="3 mm [THT]"]
  LED2 = LED - 3mm [color="Red (633nm)" package="3 mm [THT]"]
  R7 = Resistor [tolerance=±5% resistance=220 package=THT]
  R8 = Resistor [tolerance=±5% resistance=220 package=THT]
  Start = LED - 3mm [color="Red (633nm)" package="3 mm [THT]"]
  Idle = LED - 3mm [color="Red (633nm)" package="3 mm [THT]"]
  5V = Power Jack [package=power_jack_pth]
  74HC245 = IC, DIP package, 20 pins [chip_label=74HC245]
  Servo = male pin header, 3 pins [form="♂ (male)"]
  USB_Bus_Power = male pin header, 2 pins [form="♂ (male)"]
  Ground = male pin header, 4 pins [form="♂ (male)"]
  C2 = Capacitor [package=cap-pth-small2]
  Power_Switch = male pin header, 4 pins [form="♂ (male)"]
  J1 = male pin header, 2 pins [form="♂ (male)"]
  Aux_/_Headphone = male pin header, 2 pins [form="♂ (male)"]
  Outputs = male pin header, 8 pins [form="♂ (male)"]
  Run = LED - 3mm [color="Red (633nm)" package="3 mm [THT]"]
  R9 = Resistor [tolerance=±5% resistance=220 package=THT]
  PoE = Power Jack [package=power_jack_pth]
  4N35 = Optocoupler [package=THT]
  4N35_2 = Optocoupler [package=THT]
  Console_Power = male pin header, 2 pins [form="♂ (male)" part_number=PoE]

nets:
  GND: Teensy_3_2.GND, C1.-, Start.cathode, Idle.cathode, 5V.GND, 5V.GNDBREAK, 74HC245.pin10, 74HC245.pin19, Servo.pin3, Ground.pin1, Ground.pin2, Ground.pin3, Ground.pin4, C2.2, Power_Switch.pin2, Power_Switch.pin3, J1.pin2, Aux_/_Headphone.pin1, Run.cathode, 4N35.Pin_4, 4N35_2.Pin_4
  N1: Teensy_3_2.D1, Power_Switch.pin1
  N2: Teensy_3_2.D2, Power_Switch.pin4
  N3: Teensy_3_2.D3, Aux_/_Headphone.pin2
  N4: Teensy_3_2.D5, R4.Pin_0, 4N35.Pin_5
  N5: Teensy_3_2.D10, R3.Pin_0, 4N35_2.Pin_5
  N6: Teensy_3_2.A2/D16, 74HC245.pin9
  N7: Teensy_3_2.A3/D17, 74HC245.pin8
  N8: Teensy_3_2.A4/D18, 74HC245.pin7
  N9: Teensy_3_2.A5/D19, 74HC245.pin6
  N10: Teensy_3_2.A6/D20, 74HC245.pin5
  N11: Teensy_3_2.A7/D21, 74HC245.pin4
  N12: Teensy_3_2.A8/D22, 74HC245.pin3
  N13: Teensy_3_2.A9/D23, 74HC245.pin2
  N14: Teensy_3_2.3V3, R3.Pin_1, R4.Pin_1
  N15: Teensy_3_2.Vin, C1.+, 5V.PWR, 74HC245.pin1, 74HC245.pin20, Servo.pin2, C2.1, J1.pin1
  N16: R1.Pin_0, R8.Pin_0, USB_Bus_Power.pin1
  N17: R1.Pin_1, 4N35.Pin_1
  N18: R2.Pin_0, R7.Pin_0, PoE.PWR, Console_Power.pin1
  N19: R2.Pin_1, 4N35_2.Pin_1
  N20: R5.Pin_0, 74HC245.pin16
  N21: R5.Pin_1, Start.anode, Outputs.pin3
  N22: R6.Pin_0, 74HC245.pin17
  N23: R6.Pin_1, Idle.anode, Outputs.pin2
  N24: R4_2.Pin_0, 74HC245.pin15
  N25: R4_2.Pin_1, Outputs.pin4, Run.anode
  N26: LED1.cathode, USB_Bus_Power.pin2, 4N35.Pin_2
  N27: LED1.anode, R8.Pin_1
  N28: LED2.cathode, PoE.GND, PoE.GNDBREAK, 4N35_2.Pin_2, Console_Power.pin2
  N29: LED2.anode, R7.Pin_1
  N30: 74HC245.pin11, Outputs.pin8
  N31: 74HC245.pin12, Outputs.pin7
  N32: 74HC245.pin13, Outputs.pin6
  N33: 74HC245.pin14, R9.Pin_0
  N34: 74HC245.pin18, Servo.pin1, Outputs.pin1
  N35: Outputs.pin5, R9.Pin_1

notes:
  Power
  Controller
  V 1.3
  10
  1
  2
  23
  5
  16
  Romsey OrganWorks
  3
  +
  -
  Signal
