# Fritzing sketch row-power-v4 (saved by Fritzing 0.9.3b)
circuit board: 10.3505cm x 6.82996cm
breadboards: 1

parts:
  Teensy_3_2 = Teensy 3.1
  R1 = Resistor [tolerance=±5% resistance=220 package=THT]
  R3 = Resistor [tolerance=±5% resistance=220 package=THT]
  R6 = Resistor [tolerance=±5% resistance=10k package=THT]
  R4 = Resistor [tolerance=±5% resistance=10k package=THT]
  R10 = Resistor [tolerance=±5% resistance=220 package=THT]
  R9 = Resistor [tolerance=±5% resistance=220 package=THT]
  R11 = Resistor [tolerance=±5% resistance=220 package=THT]
  C1 = Capacitor Polarized [package=cpol-radial-100uf-25v]
  Start = LED - 3mm [color="Red (633nm)" package="3 mm [THT]"]
  Idle = LED - 3mm [color="Red (633nm)" package="3 mm [THT]"]
  5V = Power Jack [package=power_jack_pth]
  74HC245 = IC, DIP package, 20 pins [chip_label=74HC245]
  Servo = male pin header, 3 pins [form="♂ (male)"]
  Ground = male pin header, 4 pins [form="♂ (male)"]
  C2 = Capacitor [package=cap-pth-small2]
  Power_Switch = male pin header, 4 pins [form="♂ (male)"]
  Outputs = male pin header, 8 pins [form="♂ (male)"]
  Run = LED - 3mm [color="Red (633nm)" package="3 mm [THT]"]
  R12 = Resistor [tolerance=±5% resistance=220 package=THT]
  PoE = Power Jack [package=power_jack_pth]
  Bus = Optocoupler [package=THT]
  Cons = Optocoupler [package=THT]
  off = Optocoupler [package=THT]
  R7 = Resistor [tolerance=±5% resistance=220 package=THT]
  Opto-Out = male pin header, 3 pins [form="♂ (male)"]
  Ready = Optocoupler [package=THT]
  Inputs = male pin header, 8 pins [form="♂ (male)"]
  R2 = Resistor [tolerance=±5% resistance=220 package=THT]
  R5 = Resistor [tolerance=±5% resistance=10k package=THT]
  D1 = Rectifier Diode [part_number=1N4001 package="300 mil [THT]"]
  TIP120 = TIP120 Hi-Current Darlington Transistor
  R8 = Resistor [tolerance=±5% resistance=220 package=THT]
  Solenoid = male pin header, 3 pins [form="♂ (male)"]
  J1 = male pin header, 3 pins [form="♂ (male)"]
  B_GND_to_Ready = male pin header, 2 pins [form="♂ (male)"]
  B_GND_to_Off = male pin header, 2 pins [form="♂ (male)"]

nets:
  GND: Teensy_3_2.GND, C1.-, Start.cathode, Idle.cathode, 5V.GND, 5V.GNDBREAK, 74HC245.pin10, 74HC245.pin19, Servo.pin3, Ground.pin1, Ground.pin2, Ground.pin3, Ground.pin4, C2.2, Power_Switch.pin2, Power_Switch.pin3, Run.cathode, Bus.Pin_4, Cons.Pin_4, off.Pin_2, Ready.Pin_4, Inputs.pin2, TIP120.EMITTER, J1.pin1, J1.pin3
  N1: Teensy_3_2.D1, Power_Switch.pin1
  N2: Teensy_3_2.D2, Power_Switch.pin4
  N3: Teensy_3_2.D3, Inputs.pin1
  N4: Teensy_3_2.D5, R4.Pin_0, Bus.Pin_5
  N5: Teensy_3_2.D7, Ready.Pin_5, R5.Pin_0
  N6: Teensy_3_2.D10, R6.Pin_0, Cons.Pin_5
  N7: Teensy_3_2.A1/D15, R7.Pin_0
  N8: Teensy_3_2.A2/D16, 74HC245.pin9
  N9: Teensy_3_2.A3/D17, 74HC245.pin8
  N10: Teensy_3_2.A4/D18, 74HC245.pin7
  N11: Teensy_3_2.A5/D19, 74HC245.pin6
  N12: Teensy_3_2.A6/D20, 74HC245.pin5
  N13: Teensy_3_2.A7/D21, 74HC245.pin4
  N14: Teensy_3_2.A8/D22, 74HC245.pin3
  N15: Teensy_3_2.A9/D23, 74HC245.pin2
  N16: Teensy_3_2.3V3, R6.Pin_1, R4.Pin_1, R5.Pin_1
  N17: Teensy_3_2.Vin, C1.+, 5V.PWR, 74HC245.pin1, 74HC245.pin20, Servo.pin2, C2.1, D1.cathode, Solenoid.pin2, J1.pin2
  N18: R1.Pin_0, Inputs.pin3
  N19: R1.Pin_1, Bus.Pin_1
  N20: R3.Pin_0, PoE.PWR, Inputs.pin7
  N21: R3.Pin_1, Cons.Pin_1
  N22: R10.Pin_0, 74HC245.pin16
  N23: R10.Pin_1, Start.anode, Outputs.pin3
  N24: R9.Pin_0, 74HC245.pin17
  N25: R9.Pin_1, Idle.anode, Outputs.pin2
  N26: R11.Pin_0, 74HC245.pin15
  N27: R11.Pin_1, Outputs.pin4, Run.anode
  N28: 74HC245.pin11, Outputs.pin8
  N29: 74HC245.pin12, Outputs.pin7
  N30: 74HC245.pin13, Outputs.pin6
  N31: 74HC245.pin14, R12.Pin_0
  N32: 74HC245.pin18, Servo.pin1, Outputs.pin1, R8.Pin_0
  N33: Outputs.pin5, R12.Pin_1
  N34: PoE.GND, PoE.GNDBREAK, Cons.Pin_2, Inputs.pin8
  N35: Bus.Pin_2, Inputs.pin4, B_GND_to_Ready.pin1, B_GND_to_Off.pin1
  N36: off.Pin_1, R7.Pin_1
  N37: off.Pin_4, Opto-Out.pin1, Opto-Out.pin3, B_GND_to_Off.pin2
  N38: off.Pin_5, Opto-Out.pin2
  N39: Ready.Pin_1, R2.Pin_1
  N40: Ready.Pin_2, Inputs.pin6, B_GND_to_Ready.pin2
  N41: Inputs.pin5, R2.Pin_0
  N42: D1.anode, TIP120.COLLECTOR, Solenoid.pin1, Solenoid.pin3
  N43: TIP120.BASE, R8.Pin_1

notes:
  Power Controller V1.4
  10
  1
  2
  23
  5
  16
  Romsey OrganWorks
  3
  +
  B
  -
  15
  - (comm)
  R
  C
  A
  Sig
  7
