# Fritzing sketch simple-led-driver-v3 (saved by Fritzing 0.9.3b)
circuit board: 7.65476cm x 5.50694cm
breadboards: 1

parts:
  HCF4094 = IC, DIP package, 16 pins [chip_label=HCF4094]
  C1 = Capacitor [package=cap-pth-small2]
  From_J21 = shrouded pin header, 20 pins [form="♂ (shrouded male)"]
  J1 = female pin header, 8 pins [form="♀ (female)"]
  GND = female pin header, 4 pins [form="♀ (female)"]
  ULN2803A = IC, DIP package, 18 pins [chip_label=IC]
  Res_Array = IC, DIP package, 16 pins [chip_label=HCF4094]
  Out = female pin header, 8 pins [form="♀ (female)"]
  J2 = female pin header, 8 pins [form="♀ (female)"]
  5V = female pin header, 4 pins [form="♀ (female)"]
  Ser_In = female pin header, 5 pins [form="♀ (female)"]
  Ser_Out = female pin header, 5 pins [form="♀ (female)"]
  Clamp = Screw terminal - 2 pins [package=THT]

nets:
  N1: HCF4094.pin1, From_J21.pin17, Ser_In.pin3, Ser_Out.pin3
  N2: HCF4094.pin2, From_J21.pin18, Ser_In.pin4
  N3: HCF4094.pin3, From_J21.pin20, Ser_In.pin5, Ser_Out.pin5
  N4: HCF4094.pin4, J1.pin8, ULN2803A.pin8
  N5: HCF4094.pin5, J1.pin7, ULN2803A.pin7
  N6: HCF4094.pin6, J1.pin6, ULN2803A.pin6
  N7: HCF4094.pin7, J1.pin5, ULN2803A.pin5
  N8: HCF4094.pin8, C1.1, From_J21.pin2, From_J21.pin3, From_J21.pin4, From_J21.pin5, From_J21.pin7, From_J21.pin8, From_J21.pin9, From_J21.pin10, GND.pin1, GND.pin2, GND.pin3, GND.pin4, ULN2803A.pin9, Ser_In.pin1, Ser_Out.pin1, Clamp.pin2
  N9: HCF4094.pin9, Ser_Out.pin4
  N10: HCF4094.pin11, J1.pin1, ULN2803A.pin1
  N11: HCF4094.pin12, J1.pin2, ULN2803A.pin2
  N12: HCF4094.pin13, J1.pin3, ULN2803A.pin3
  N13: HCF4094.pin14, J1.pin4, ULN2803A.pin4
  N14: HCF4094.pin15, HCF4094.pin16, C1.2, From_J21.pin1, From_J21.pin6, 5V.pin1, 5V.pin2, 5V.pin3, 5V.pin4, Ser_In.pin2, Ser_Out.pin2
  N15: ULN2803A.pin10, Clamp.pin1
  N16: ULN2803A.pin11, Res_Array.pin8, J2.pin8
  N17: ULN2803A.pin12, Res_Array.pin7, J2.pin7
  N18: ULN2803A.pin13, Res_Array.pin6, J2.pin6
  N19: ULN2803A.pin14, Res_Array.pin5, J2.pin5
  N20: ULN2803A.pin15, Res_Array.pin4, J2.pin4
  N21: ULN2803A.pin16, Res_Array.pin3, J2.pin3
  N22: ULN2803A.pin17, Res_Array.pin2, J2.pin2
  N23: ULN2803A.pin18, Res_Array.pin1, J2.pin1
  N24: Res_Array.pin9, Out.pin8
  N25: Res_Array.pin10, Out.pin7
  N26: Res_Array.pin11, Out.pin6
  N27: Res_Array.pin12, Out.pin5
  N28: Res_Array.pin13, Out.pin4
  N29: Res_Array.pin14, Out.pin3
  N30: Res_Array.pin15, Out.pin2
  N31: Res_Array.pin16, Out.pin1

notes:
  clock
  data
  latch
  Romsey Organworks
  LED Output
  1
  8
